# Fritzing sketch motion_sensor (saved by Fritzing 0.9.1b)
breadboards: 1

parts:
  パーツ1 = Arduino Uno (Rev3)
  LED1 = LED - 5mm [color="Red (633nm)" package="5 mm [THT]"]
  PIR1 = PIR sensor
  U1 = Voltage Regulator - 5V [package="DPak [SMD]"]
  0_1u = Capacitor [package=cap-pth-small]
  VCC1 = Battery block 9V
  0_1u_2 = Capacitor [package=cap-pth-small]
  0_2u = Capacitor [package=cap-pth-small]

nets:
  GND: パーツ1.GND, LED1.cathode, PIR1.GND, U1.GND, 0_1u.2, 0_1u_2.2, 0_2u.2
  N1: パーツ1.D2, PIR1.SIG
  N2: パーツ1.D6_PWM, LED1.anode
  5V: パーツ1.5V, PIR1.VDD, U1.output_voltage
  N3: U1.input_voltage, VCC1.+, 0_1u_2.1, 0_2u.1
  N4: 0_1u.1, VCC1.-
